# Fritzing sketch breadboard (saved by Fritzing 0.9.4)
breadboards: 1

parts:
  A1 = Waveshare rp2040-zero tht [package=THT]
  Part1 = NRF24L01+ Breakout Board
  U1 = mystery part, 3 pins [chip_label=3.3V]

nets:
  N1: A1.Pin_1, U1.pin1
  N2: A1.Pin_2, Part1.GND, U1.pin3
  N3: A1.Pin_18, Part1.CE
  N4: A1.Pin_19, Part1.MISO
  N5: A1.Pin_20, Part1.MOSI
  N6: A1.Pin_21, Part1.SCK
  N7: A1.Pin_22, Part1.CS
  N8: Part1.VCC, U1.pin2

custom parts:
  Waveshare rp2040-zero tht: .RP2040-Zero, A Low-Cost, High-Performance Pico-Like MCU Board Based On Raspberry Pi Microcontroller RP2040. This varant is THT without the extra connections.
